# Fritzing sketch hw-sketch (saved by Fritzing 0.9.3b)
circuit board: 6.3116cm x 4.49422cm
breadboards: 1

parts:
  LED1 = LED - 5mm [color="Infrared (940nm)" current=100mA package="5 mm [THT]"]
  R1 = Resistor [tolerance=±20% resistance=1k package=THT]
  R2 = Resistor [tolerance=±5% resistance=47 package=THT]
  WeMos_D1_Mini1 = WeMos D1 Mini
  DHT22_/_AM2303 = Humidity and Temperature Sensor RHT03
  R3 = Resistor [tolerance=±5% resistance=150 package=THT]
  R4 = Resistor [tolerance=±1% resistance=100 package=THT]
  R5 = Resistor [tolerance=±5% resistance=100 package=THT]
  Micro_SD_Card = Header 6 [package=1x06-smd-female-v2]
  Q1 = NPN-Transistor [part_number="2N 3904" package="TO92 [THT]"]
  LED2 = RGB LED (com. cathode, rbg) [package="5 mm [THT]"]

nets:
  N1: LED1.cathode, Q1.C
  N2: LED1.anode, R2.Pin_0
  N3: R1.Pin_0, Q1.B
  N4: R1.Pin_1, WeMos_D1_Mini1.D8
  N5: R2.Pin_1, WeMos_D1_Mini1.5V, LED2.common_cathode
  3V3: WeMos_D1_Mini1.3V3, DHT22_/_AM2303.Vcc, Micro_SD_Card.3V3
  N6: WeMos_D1_Mini1.D0, R5.Pin_1
  N7: WeMos_D1_Mini1.D1, DHT22_/_AM2303.Data-signal
  N8: WeMos_D1_Mini1.D2, R4.Pin_1
  N9: WeMos_D1_Mini1.D3, R3.Pin_1
  N10: WeMos_D1_Mini1.D4, Micro_SD_Card.CS
  N11: WeMos_D1_Mini1.D5, Micro_SD_Card.CLX
  N12: WeMos_D1_Mini1.D6, Micro_SD_Card.MISO
  N13: WeMos_D1_Mini1.D7, Micro_SD_Card.MOSI
  N14: WeMos_D1_Mini1.G, DHT22_/_AM2303.GND_1, DHT22_/_AM2303.GND_2, Micro_SD_Card.GND, Q1.E
  N15: R3.Pin_0, LED2.red_anode
  N16: R4.Pin_0, LED2.blue_anode
  N17: R5.Pin_0, LED2.green_anode

notes:
  D1 Mini
  D5: CLK (Clock)
  D6: MISO
  D7: MOSI
  D4: CS

custom parts:
  Header 6: Header 6 Standard 6-pin 0.1 header. Use with straight break away headers (SKU : PRT-00116), right angle break away headers (PRT-00553), swiss pins (PRT-00743), machine pins (PRT-00117), and female headers (PRT-00115). Molex polarized connector foot print use with SKU : PRT-08094 with associated crimp pins and housings. NOTES ON THE VARIANTS LOCK and LOCK_LONGPADS... This footprint was designed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
